// Logisim project FLIP FLOP.circ as structural Verilog: 2 circuits, main circuit main
module main (
  input  in_1,
  input  in_2,
  output out_3,
  output out_4
);

  wire nand_1_out, nand_2_out;

  nand nand_1 (nand_1_out, in_1, in_2);
  nand nand_2 (nand_2_out, nand_1_out, in_2);
  nand nand_3 (out_3, nand_1_out, out_4);
  nand nand_4 (out_4, out_3, nand_2_out);
endmodule

module D_FLIP_FLOP (
);

  main main_1 ();  // open: in_1, in_2, out_3, out_4

  // Notes on the sheet:
  //   D-flip flop
endmodule
